# Fritzing sketch Stellpultv2-LED (saved by Fritzing 0.9.9b)
circuit board: 6.03743cm x 5.4748cm
breadboards: 1

parts:
  Main = Header 4 [package=jst-4-pth]
  IC1 = SO-24W [chip_label=IC part_number=PCA9555 package=SO(w)]
  LED_1-8 = double row male pin header, 16 pins [form="♂ (male)"]
  LED_9-16 = double row male pin header, 16 pins [form="♂ (male)"]
  R1 = Resistor [tolerance=±5% resistance=220 power=0.25 package="1206 [SMD]"]
  R2 = Resistor [tolerance=±5% resistance=220 power=0.25 package="1206 [SMD]"]
  R3 = Resistor [tolerance=±5% resistance=220 power=0.25 package="1206 [SMD]"]
  R4 = Resistor [tolerance=±5% resistance=220 power=0.25 package="1206 [SMD]"]
  R10 = Resistor [tolerance=±5% resistance=220 power=0.25 package="1206 [SMD]"]
  R12 = Resistor [tolerance=±5% resistance=220 power=0.25 package="1206 [SMD]"]
  R13 = Resistor [tolerance=±5% resistance=220 power=0.25 package="1206 [SMD]"]
  R16 = Resistor [tolerance=±5% resistance=220 power=0.25 package="1206 [SMD]"]
  LED_1-6_inv = double row male pin header, 12 pins [form="♂ (male)"]
  R17 = Resistor [tolerance=±5% resistance=220 power=0.25 package="1206 [SMD]"]
  R19 = Resistor [tolerance=±5% resistance=220 power=0.25 package="1206 [SMD]"]
  R20 = Resistor [tolerance=±5% resistance=220 power=0.25 package="1206 [SMD]"]
  R21 = Resistor [tolerance=±5% resistance=220 power=0.25 package="1206 [SMD]"]
  R8 = Resistor [tolerance=±5% resistance=220 power=0.25 package="1206 [SMD]"]
  R6 = Resistor [tolerance=±5% resistance=220 power=0.25 package="1206 [SMD]"]
  R7 = Resistor [tolerance=±5% resistance=220 power=0.25 package="1206 [SMD]"]
  R5 = Resistor [tolerance=±5% resistance=220 power=0.25 package="1206 [SMD]"]
  IC2 = SO14 [chip_label=IC package=SO]
  R18 = Resistor [tolerance=±5% resistance=220 power=0.25 package="1206 [SMD]"]
  R22 = Resistor [tolerance=±5% resistance=220 power=0.25 package="1206 [SMD]"]
  R15 = Resistor [tolerance=±5% resistance=220 power=0.25 package="1206 [SMD]"]
  R9 = Resistor [tolerance=±5% resistance=220 power=0.25 package="1206 [SMD]"]
  R14 = Resistor [tolerance=±5% resistance=220 power=0.25 package="1206 [SMD]"]
  R11 = Resistor [tolerance=±5% resistance=220 power=0.25 package="1206 [SMD]"]

nets:
  N1: Main.1, IC1.21, IC1.24, IC2.14
  N2: Main.2, IC1.23
  N3: Main.3, IC1.22
  GND: Main.4, IC1.2, IC1.3, IC1.12, LED_1-8.pin1, LED_1-8.pin2, LED_1-8.pin3, LED_1-8.pin4, LED_1-8.pin5, LED_1-8.pin6, LED_1-8.pin7, LED_1-8.pin8, LED_9-16.pin9, LED_9-16.pin10, LED_9-16.pin11, LED_9-16.pin12, LED_9-16.pin13, LED_9-16.pin14, LED_9-16.pin15, LED_9-16.pin16, LED_1-6_inv.pin1, LED_1-6_inv.pin2, LED_1-6_inv.pin3, LED_1-6_inv.pin4, LED_1-6_inv.pin5, LED_1-6_inv.pin6, IC2.7
  N4: IC1.4, R4.Pin_1, IC2.1
  N5: IC1.5, R3.Pin_1, IC2.3
  N6: IC1.6, R2.Pin_1, IC2.5
  N7: IC1.7, R1.Pin_1, IC2.9
  N8: IC1.8, R8.Pin_1, IC2.11
  N9: IC1.9, R6.Pin_1, IC2.13
  N10: IC1.10, R7.Pin_1
  N11: IC1.11, R5.Pin_1
  N12: IC1.13, R16.Pin_1
  N13: IC1.14, R13.Pin_1
  N14: IC1.15, R12.Pin_1
  N15: IC1.16, R10.Pin_1
  N16: IC1.17, R15.Pin_1
  N17: IC1.18, R9.Pin_1
  N18: IC1.19, R14.Pin_1
  N19: IC1.20, R11.Pin_1
  N20: LED_1-8.pin9, R5.Pin_0
  N21: LED_1-8.pin10, R7.Pin_0
  N22: LED_1-8.pin11, R6.Pin_0
  N23: LED_1-8.pin12, R8.Pin_0
  N24: LED_1-8.pin13, R1.Pin_0
  N25: LED_1-8.pin14, R2.Pin_0
  N26: LED_1-8.pin15, R3.Pin_0
  N27: LED_1-8.pin16, R4.Pin_0
  N28: LED_9-16.pin1, R11.Pin_0
  N29: LED_9-16.pin2, R14.Pin_0
  N30: LED_9-16.pin3, R9.Pin_0
  N31: LED_9-16.pin4, R15.Pin_0
  N32: LED_9-16.pin5, R10.Pin_0
  N33: LED_9-16.pin6, R12.Pin_0
  N34: LED_9-16.pin7, R13.Pin_0
  N35: LED_9-16.pin8, R16.Pin_0
  N36: LED_1-6_inv.pin7, R21.Pin_0
  N37: LED_1-6_inv.pin8, R19.Pin_0
  N38: LED_1-6_inv.pin9, R17.Pin_0
  N39: LED_1-6_inv.pin10, R20.Pin_0
  N40: LED_1-6_inv.pin11, R18.Pin_0
  N41: LED_1-6_inv.pin12, R22.Pin_0
  N42: R17.Pin_1, IC2.8
  N43: R19.Pin_1, IC2.10
  N44: R20.Pin_1, IC2.6
  N45: R21.Pin_1, IC2.12
  N46: IC2.2, R22.Pin_1
  N47: IC2.4, R18.Pin_1

notes:
  ZBahn Stellpult v1.1 LED
