# Fritzing sketch Stellpultv2-Main (saved by Fritzing 0.9.9b)
circuit board: 8.82023cm x 5.64444cm
breadboards: 1

parts:
  Arduino_UNO = Arduino Uno (Rev3)
  J1 = male pin header, 2 pins [form="♂ (male)"]
  D1 = Diode [package=diode-1n4001]
  C3 = Capacitor [part_number=100nF package=0805]
  U1 = RJ11 Jack [package=rj11-6]
  IC1 = SO08 [chip_label="IC MAX485" package=SO]
  C4 = Capacitor [part_number=100nF package=0805]
  R2 = Resistor [tolerance=±5% resistance=1.5k power=0.25 package="1206 [SMD]"]
  R3 = Resistor [tolerance=±5% power=0.25 resistance=120 package=THT]
  IC2 = SO-24W [chip_label=IC part_number=PCA9555 package=SO(w)]
  R5 = Resistor [tolerance=±5% resistance=10k power=0.25 package="1206 [SMD]"]
  Schalter_1-8 = double row male pin header, 16 pins [form="♂ (male)"]
  Schalter_9-16 = double row male pin header, 16 pins [form="♂ (male)"]
  R6 = Resistor [tolerance=±5% resistance=10k power=0.25 package="1206 [SMD]"]
  R4 = Resistor [tolerance=±5% resistance=470 power=0.25 package="1206 [SMD]"]
  LED = Header 4 [package=jst-4-pth]
  Display = Header 4 [package=jst-4-pth]
  R1 = Resistor [tolerance=±5% resistance=1.5k power=0.25 package="1206 [SMD]"]
  LED1 = LED - 3mm [color="Red (633nm)" current=0.030 package="3 mm [THT]"]
  Key = Header 4 [package=jst-4-pth]
  Int = male pin header, 2 pins [form="♂ (male)"]
  SD_Card = double row male pin header, 6 pins [form="♂ (male)"]

nets:
  N1: Arduino_UNO.A4/SDA, IC2.23, R6.Pin_0, LED.2, Display.2, Key.2
  N2: Arduino_UNO.A5/SCL, IC2.22, R5.Pin_0, LED.3, Display.3
  N3: Arduino_UNO.D9_PWM, IC1.2, IC1.3, R4.Pin_0
  N4: Arduino_UNO.D11_PWM/MOSI, SD_Card.pin3
  N5: Arduino_UNO.D12/MISO, SD_Card.pin4
  N6: Arduino_UNO.D13/SCK, SD_Card.pin2
  GND: Arduino_UNO.GND, C3.2, U1.2, IC1.5, C4.1, R2.Pin_1, IC2.2, IC2.3, IC2.12, IC2.21, Schalter_1-8.pin9, Schalter_1-8.pin10, Schalter_1-8.pin11, Schalter_1-8.pin12, Schalter_1-8.pin13, Schalter_1-8.pin14, Schalter_1-8.pin15, Schalter_1-8.pin16, Schalter_9-16.pin1, Schalter_9-16.pin2, Schalter_9-16.pin3, Schalter_9-16.pin4, Schalter_9-16.pin5, Schalter_9-16.pin6, Schalter_9-16.pin7, Schalter_9-16.pin8, LED.4, Display.4, SD_Card.pin1, SD_Card.pin6
  N7: Arduino_UNO.D0/RX, IC1.1
  N8: Arduino_UNO.D1/TX, IC1.4
  N9: Arduino_UNO.D2, IC2.1, Int.pin1
  N10: Arduino_UNO.D3_PWM, Int.pin2
  5V: Arduino_UNO.5V, IC1.8, C4.2, IC2.24, R5.Pin_1, R6.Pin_1, LED.1, Display.1, R1.Pin_0, LED1.anode, Key.1, SD_Card.pin5
  N11: Arduino_UNO.VIN, J1.pin1
  N12: J1.pin2, D1.C
  N13: D1.A, C3.1, U1.5
  N14: U1.3, IC1.7, R2.Pin_0, R3.Pin_1
  N15: U1.4, IC1.6, R3.Pin_0, R1.Pin_1
  N16: IC2.4, Schalter_1-8.pin8
  N17: IC2.5, Schalter_1-8.pin7
  N18: IC2.6, Schalter_1-8.pin6
  N19: IC2.7, Schalter_1-8.pin5
  N20: IC2.8, Schalter_1-8.pin4
  N21: IC2.9, Schalter_1-8.pin3
  N22: IC2.10, Schalter_1-8.pin2
  N23: IC2.11, Schalter_1-8.pin1
  N24: IC2.13, Schalter_9-16.pin16
  N25: IC2.14, Schalter_9-16.pin15
  N26: IC2.15, Schalter_9-16.pin14
  N27: IC2.16, Schalter_9-16.pin13
  N28: IC2.17, Schalter_9-16.pin12
  N29: IC2.18, Schalter_9-16.pin11
  N30: IC2.19, Schalter_9-16.pin10
  N31: IC2.20, Schalter_9-16.pin9
  N32: R4.Pin_1, LED1.cathode

notes:
  ZBahn Stellpult v1.1
